# Fritzing sketch Wiring Diagram (saved by Fritzing 0.9.5d)
breadboards: 1

parts:
  A2 = ESP32-S3 devkit 1
  RS1 = RS232 Shield  # not connected
  RS2 = RS232 Shield
  ZS-042_RTC1 = ZS-042 RTC Module  # not connected
  Part1 = LCD1602-I2C  # not connected
  S1 = Round Pushbutton  # not connected
  J1 = XL4015 DC-DC CC CV module (blue)

nets:
  N1: A2.Pin_1, A2.Pin_42, RS2.GND, J1.pin_4
  N2: A2.Pin_2, RS2.VCC
  N3: A2.Pin_22, J1.pin_3

custom parts:
  ESP32-S3 devkit 1: ESP32-S3-DevKitC-1 Development Board BT 2.4G Wifi Module for Arduino 8MB PSRAM 16MB FLASH N16R8 42Pin CH340C Type-C ESP32 S3.
  RS232 Shield: RS232 connector, 4-pin, right-angle female. Designed by Dr Kristofer Chan, King's College London / remote-research.org. Licensed under Creative Commons Attribution-ShareAlike 4.0
  LCD1602-I2C: A standard character display, usually with 2x16 characters. Comes in many colors with LCM1602 IIC attached.
  XL4015 DC-DC CC CV module (blue): XL4015 DC-DC CC/CV module blue
